# Fritzing sketch umbra-la (saved by Fritzing 0.9.3b)

parts:
  Raspberry_Pi1 = Raspberry Pi 2
  Part1 = Adafruit Si7021 Temp Humidity [part_number="Adafruit #3251"]
  LCD1 = LCD screen
  Part2 = MPL3115A2 I2C Barometric Pressure, Altitude, Temperature Sensor
  Part3 = Adafruit TSL2591 [part_number="Adafruit #1980"]
  U1 = POT [package=pot_alpha_rv16af-20]

nets:
  3.3V: Raspberry_Pi1.3v3, Part1.VIN, Part2.VIN, Part3.VIN
  SDA: Raspberry_Pi1.GPIO2, Part1.SDA, Part2.SDA, Part3.SDA
  SCL: Raspberry_Pi1.GPIO3, Part1.SCL, Part2.SCL, Part3.SCL
  GND: Raspberry_Pi1.GND, Part1.GND, LCD1.VSS, LCD1.R/W, LCD1.LED-, Part2.GND, Part3.GND, U1.A
  N1: Raspberry_Pi1.GPIO17, LCD1.DB5
  N2: Raspberry_Pi1.GPIO22, LCD1.DB7
  N3: Raspberry_Pi1.GPIO21, LCD1.DB6
  N4: Raspberry_Pi1.GPIO25, LCD1.RS
  N5: Raspberry_Pi1.GPIO24, LCD1.E
  N6: Raspberry_Pi1.GPIO23, LCD1.DB4
  5V/VDD: Raspberry_Pi1.5V, LCD1.VDD, LCD1.LED+, U1.E
  Vpot: LCD1.V0, U1.S

custom parts:
  Adafruit Si7021 Temp Humidity: It's summer and you're sweating and your hair's all frizzy and all you really want to know is why the weatherman said this morning that today's relative humidity would max out at a perfectly reasonable 42% when it feels more like 77%. Enter the Si7021 Temperature + Humidity Sensor - the best way to prove the weatherman wrong! This lovely sensor for Silicon labs has ± 3% relative humidity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
  MPL3115A2 I2C Barometric Pressure, Altitude, Temperature Sensor: This pressure sensor from Freescale is a great low-cost sensing solution for precision measurement of barometric pressure and altitude. The MPL3115A2 has a typical 1.5 Pascal resolution, which can resolve altitude at 0.3 meters (compare to the BMP180 which can do 0.17m). It has some upsides compared to the BMP180, such as interrupt outputs for ultra-low power usage, and its also a heck of a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
  Adafruit TSL2591: When the future is dazzlingly-bright, this ultra-high-range luminosity sensor will help you measure it. The TSL2591 luminosity sensor is an advanced digital light sensor, ideal for use in a wide range of light situations. Compared to low cost CdS cells, this sensor is more precise, allowing for exact lux calculations and can be configured for different gain/timing ranges to detect light ranges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
